// Logisim project Lab05_counter.circ as structural Verilog: 7 circuits, main circuit main
module main (
  input  Reset
);

  wire clk_out;
  wire [3:0] synchronousringcounter_1_ring;

  Clock #(.highDuration(4), .lowDuration(4)) clk (.out(clk_out));
  Clock sysclk ();  // open: out
  SynchronousRingCounter synchronousringcounter_1 (.clk(clk_out), .rst(Reset), .Ring(synchronousringcounter_1_ring));
  // Probe on synchronousringcounter_1_ring
  Hex_Digit_Display hex_digit_display_1 (.value(synchronousringcounter_1_ring));  // open: dp

  // Notes on the sheet:
  //   March 6, 2024
  //   Kamila Tashimova
  //   Lab 05: Counters
endmodule

module AsynchronousUpCounter (
  input  clk,
  input  rst,
  output [3:0] Up
);

  wire d_ff_1_qn, d_ff_2_qn, d_ff_3_qn, d_ff_4_qn;

  D_Flip_Flop d_ff_1 (.D(d_ff_1_qn), .clk(clk), .Q(Up[0]), .Qn(d_ff_1_qn), .reset(rst));  // open: preset
  D_Flip_Flop d_ff_2 (.D(d_ff_2_qn), .clk(d_ff_1_qn), .Q(Up[1]), .Qn(d_ff_2_qn), .reset(rst));  // open: preset
  D_Flip_Flop d_ff_3 (.D(d_ff_3_qn), .clk(d_ff_2_qn), .Q(Up[2]), .Qn(d_ff_3_qn), .reset(rst));  // open: preset
  D_Flip_Flop d_ff_4 (.D(d_ff_4_qn), .clk(d_ff_3_qn), .Q(Up[3]), .Qn(d_ff_4_qn), .reset(rst));  // open: preset
endmodule

module AsynchronousDownCounter (
  input  clk,
  input  rst,
  output [3:0] Down
);

  wire d_ff_1_qn, d_ff_2_qn, d_ff_3_qn, d_ff_4_qn;

  D_Flip_Flop d_ff_1 (.D(d_ff_1_qn), .clk(clk), .Q(Down[0]), .Qn(d_ff_1_qn), .preset(rst));  // open: reset
  D_Flip_Flop d_ff_2 (.D(d_ff_2_qn), .clk(Down[0]), .Q(Down[1]), .Qn(d_ff_2_qn), .preset(rst));  // open: reset
  D_Flip_Flop d_ff_3 (.D(d_ff_3_qn), .clk(Down[1]), .Q(Down[2]), .Qn(d_ff_3_qn), .preset(rst));  // open: reset
  D_Flip_Flop d_ff_4 (.D(d_ff_4_qn), .clk(Down[2]), .Q(Down[3]), .Qn(d_ff_4_qn), .preset(rst));  // open: reset
endmodule

module AsynchronousDecadeCounter (
  input  clk,
  input  rst,
  output [3:0] Decade
);

  wire and_1_out, d_ff_1_qn, d_ff_2_qn, d_ff_3_qn, d_ff_4_qn, or_1_out;

  D_Flip_Flop d_ff_1 (.D(d_ff_1_qn), .clk(clk), .Q(Decade[0]), .Qn(d_ff_1_qn), .reset(or_1_out));  // open: preset
  or or_1 (or_1_out, rst, and_1_out);
  D_Flip_Flop d_ff_2 (.D(d_ff_2_qn), .clk(d_ff_1_qn), .Q(Decade[1]), .Qn(d_ff_2_qn), .reset(or_1_out));  // open: preset
  D_Flip_Flop d_ff_3 (.D(d_ff_3_qn), .clk(d_ff_2_qn), .Q(Decade[2]), .Qn(d_ff_3_qn), .reset(or_1_out));  // open: preset
  D_Flip_Flop d_ff_4 (.D(d_ff_4_qn), .clk(d_ff_3_qn), .Q(Decade[3]), .Qn(d_ff_4_qn), .reset(or_1_out));  // open: preset
  and and_1 (and_1_out, Decade[3], Decade[1]);
endmodule

module SynchronousRingCounter (
  input  clk,
  input  rst,
  output [3:0] Ring
);

  D_Flip_Flop d_ff_1 (.D(Ring[3]), .clk(clk), .Q(Ring[0]), .preset(rst));  // open: Qn, reset
  D_Flip_Flop d_ff_2 (.D(Ring[0]), .clk(clk), .Q(Ring[1]), .reset(rst));  // open: Qn, preset
  D_Flip_Flop d_ff_3 (.D(Ring[1]), .clk(clk), .Q(Ring[2]), .reset(rst));  // open: Qn, preset
  D_Flip_Flop d_ff_4 (.D(Ring[2]), .clk(clk), .Q(Ring[3]), .reset(rst));  // open: Qn, preset
endmodule

module SynchronousJonhsonCounter (
  input  clk,
  input  rst,
  output [3:0] Jonhson
);

  wire d_ff_4_qn;

  D_Flip_Flop d_ff_1 (.D(d_ff_4_qn), .clk(clk), .Q(Jonhson[0]), .preset(rst));  // open: Qn, reset
  D_Flip_Flop d_ff_2 (.D(Jonhson[0]), .clk(clk), .Q(Jonhson[1]), .reset(rst));  // open: Qn, preset
  D_Flip_Flop d_ff_3 (.D(Jonhson[1]), .clk(clk), .Q(Jonhson[2]), .reset(rst));  // open: Qn, preset
  D_Flip_Flop d_ff_4 (.D(Jonhson[2]), .clk(clk), .Q(Jonhson[3]), .Qn(d_ff_4_qn), .reset(rst));  // open: preset
endmodule

module Universal (
  input  clk,
  input  Reset,
  input  [2:0] in_3,
  output [3:0] out_4
);

  wire [3:0] asynchronousdecadecounter_1_decade, asynchronousdowncounter_1_down, asynchronousupcounter_1_up,
       synchronousjonhsoncounter_1_jonhson, synchronousringcounter_1_ring;

  AsynchronousUpCounter asynchronousupcounter_1 (.clk(clk), .rst(Reset), .Up(asynchronousupcounter_1_up));
  AsynchronousDownCounter asynchronousdowncounter_1 (.clk(clk), .rst(Reset), .Down(asynchronousdowncounter_1_down));
  AsynchronousDecadeCounter asynchronousdecadecounter_1 (
    .clk(clk), .rst(Reset), .Decade(asynchronousdecadecounter_1_decade));
  SynchronousRingCounter synchronousringcounter_1 (.clk(clk), .rst(Reset), .Ring(synchronousringcounter_1_ring));
  SynchronousJonhsonCounter synchronousjonhsoncounter_1 (
    .clk(clk), .rst(Reset), .Jonhson(synchronousjonhsoncounter_1_jonhson));
  Multiplexer #(.select(3), .width(4)) multiplexer_1 (
    .in0(4'b0001), .in1(4'b0001), .in2(asynchronousupcounter_1_up), .in3(asynchronousdowncounter_1_down),
    .in4(asynchronousdecadecounter_1_decade), .in5(synchronousringcounter_1_ring),
    .in6(synchronousjonhsoncounter_1_jonhson), .in7(4'b0001), .out(out_4), .sel(in_3));
endmodule
